# Fritzing sketch Transmitter (saved by Fritzing 0.9.2b)
breadboards: 1

parts:
  Part1 = Arduino Uno (Rev3)
  LED1 = smd LED [color="Green (555nm)" package="0805 [SMD]"]
  U2 = RF-LINK_TX [package=rf-link_tx]  # not connected
  R1 = Resistor [tolerance=±5% resistance=220 package=THT]

nets:
  N1: Part1.D13/SCK, R1.Pin_1
  N2: Part1.GND, LED1.cathode
  N3: LED1.anode, R1.Pin_0

custom parts:
  RF-LINK_TX: Common RF transmitter of the 315.00Mhz varity
